// Logisim project CRC校验.circ as structural Verilog: 2 circuits, main circuit CRC
module CRC (
  input  [7:0] A,
  input  [3:0] B,
  output [10:0] out_3
);

  wire [2:0] \mod2_1_余数 , \mod2_2_余数 , \mod2_3_余数 , \mod2_4_余数 , \mod2_5_余数 , \mod2_6_余数 , \mod2_7_余数 ;

  mod2 mod2_1 (.in_1(A[7:4]), .in_2(B), .\余数 (\mod2_1_余数 ));
  mod2 mod2_2 (.in_1({\mod2_1_余数 , A[3]}), .in_2(B), .\余数 (\mod2_2_余数 ));
  mod2 mod2_3 (.in_1({\mod2_2_余数 , A[2]}), .in_2(B), .\余数 (\mod2_3_余数 ));
  mod2 mod2_4 (.in_1({\mod2_3_余数 , A[1]}), .in_2(B), .\余数 (\mod2_4_余数 ));
  mod2 mod2_5 (.in_1({\mod2_4_余数 , A[0]}), .in_2(B), .\余数 (\mod2_5_余数 ));
  mod2 mod2_6 (.in_1({\mod2_5_余数 , 1'b0}), .in_2(B), .\余数 (\mod2_6_余数 ));
  mod2 mod2_7 (.in_1({\mod2_6_余数 , 1'b0}), .in_2(B), .\余数 (\mod2_7_余数 ));
  mod2 mod2_8 (.in_1({\mod2_7_余数 , 1'b0}), .in_2(B), .\余数 (out_3[2:0]));

  assign out_3[10:3] = A;

  // Other names for the same wires on the sheet: C[10:0] = {A, out_3[2:0]}
endmodule

module mod2 (
  input  [3:0] in_1,
  input  [3:0] in_2,
  output [2:0] \余数 
);

  wire [3:0] xor_1_out;
  wire [3:3] multiplexer_1_out;

  assign xor_1_out = in_1 ^ in_2;  // XOR_Gate xor_1, 4 bits wide
  Multiplexer #(.width(4)) multiplexer_1 (
    .in0(in_1), .in1(xor_1_out), .out({multiplexer_1_out[3], \余数 }), .sel(in_1[3]));  // open: en

  // Other names for the same wires on the sheet: 被除数[3:0] = in_1; 最高位 = in_1[3]; 除数[3:0] = in_2
endmodule
