// Logisim project Logisim中的FSM.circ as structural Verilog: 2 circuits, main circuit fsm
module fsm (
  input  [1:0] in_1,
  input  in_2,
  output z
);

  wire CLK, comparator_1_eq, comparator_2_eq, comparator_3_eq, or_1_out, register_2_q;
  wire [1:0] state, \状态转移_1_out_3 ;

  Clock clock_1 (.out(CLK));
  Comparator #(.width(2), .mode("unsigned")) comparator_1 (.a(state), .b(2'b10), .eq(comparator_1_eq));  // open: gt, lt
  Comparator #(.width(2), .mode("unsigned")) comparator_2 (.a(in_1), .b(2'b00), .eq(comparator_2_eq));  // open: gt, lt
  Comparator #(.width(2), .mode("unsigned")) comparator_3 (.a(in_1), .b(2'b10), .eq(comparator_3_eq));  // open: gt, lt
  \状态转移  \u_状态转移_1  (.N(state), .IN(in_1), .out_3(\状态转移_1_out_3 ));
  Register #(.width(2)) register_1 (.D(\状态转移_1_out_3 ), .Q(state), .clk(CLK), .clr(register_2_q));  // open: en
  Register #(.width(1)) register_2 (.D(in_2), .Q(register_2_q), .clk(CLK), .clr(register_2_q));  // open: en
  or or_1 (or_1_out, comparator_2_eq, comparator_3_eq);
  // Probe on state
  and and_1 (z, comparator_1_eq, or_1_out);

  // Other names for the same wires on the sheet: CLR = in_2; In[1:0] = in_1
endmodule

module \状态转移  (
  input  [1:0] N,
  input  [1:0] IN,
  output [1:0] out_3
);

  wire and_1_out, and_2_out, and_3_out, and_4_out, not_1_out, not_2_out, not_3_out, not_4_out, not_5_out,
       not_6_out, not_7_out;

  not not_1 (not_1_out, N[1]);
  and and_1 (and_1_out, not_1_out, N[0], not_2_out);
  not not_2 (not_2_out, IN[0]);
  and and_2 (and_2_out, N[1], not_3_out, not_4_out);
  not not_3 (not_3_out, N[0]);
  not not_4 (not_4_out, IN[0]);
  not not_5 (not_5_out, IN[1]);
  and and_3 (and_3_out, not_5_out, IN[0]);
  not not_6 (not_6_out, N[0]);
  and and_4 (and_4_out, N[1], not_6_out, not_7_out);
  not not_7 (not_7_out, IN[0]);
  or or_1 (out_3[1], and_1_out, and_2_out);
  or or_2 (out_3[0], and_3_out, and_4_out);

  // Other names for the same wires on the sheet: O0 = out_3[0]; O1 = out_3[1]
endmodule
