// Logisim project Logisim导航.circ as structural Verilog: 2 circuits, main circuit navigation
module navigation (
  input  [1:0] in_1,
  input  in_2,
  input  in_3,
  output out_4,
  output out_5
);

  wire comparator_2_eq, comparator_3_eq, comparator_4_eq, comparator_5_eq;
  wire [3:0] state, \状态转移_1_out_3 ;

  // Probe on state
  \状态转移  \u_状态转移_1  (.in_1(state), .in_2(in_1), .out_3(\状态转移_1_out_3 ));
  Comparator #(.width(4), .mode("unsigned")) comparator_1 (.a(state), .b(4'b0100), .eq(out_4));  // open: gt, lt
  Comparator #(.width(4), .mode("unsigned")) comparator_2 (
    .a(state), .b(4'b0101), .eq(comparator_2_eq));  // open: gt, lt
  Comparator #(.width(4), .mode("unsigned")) comparator_3 (
    .a(state), .b(4'b0110), .eq(comparator_3_eq));  // open: gt, lt
  Comparator #(.width(4), .mode("unsigned")) comparator_4 (
    .a(state), .b(4'b0111), .eq(comparator_4_eq));  // open: gt, lt
  Comparator #(.width(4), .mode("unsigned")) comparator_5 (
    .a(state), .b(4'b1000), .eq(comparator_5_eq));  // open: gt, lt
  Register #(.width(4)) register_1 (.D(\状态转移_1_out_3 ), .Q(state), .clk(in_2), .clr(in_3));  // open: en
  or or_1 (out_5, comparator_2_eq, comparator_3_eq, comparator_4_eq, comparator_5_eq);

  // Other names for the same wires on the sheet: arrive = out_4; clk = in_2; dir[1:0] = in_1; hit = out_5;
  //   reset = in_3
endmodule

module \状态转移  (
  input  [3:0] in_1,
  input  [1:0] in_2,
  output [3:0] out_3
);

  wire and_1_out, and_2_out, and_3_out, and_4_out, and_5_out, and_6_out, and_7_out, and_8_out, and_9_out,
       and_10_out, and_11_out, and_12_out, and_13_out, and_14_out, and_15_out, and_16_out, and_17_out,
       and_18_out, and_19_out, and_20_out, and_21_out, and_22_out, and_23_out, and_24_out, and_25_out,
       and_26_out, and_27_out, and_28_out, and_29_out, and_30_out, and_31_out, and_32_out, and_33_out,
       and_34_out, and_35_out, and_36_out, and_37_out, and_38_out, and_39_out, and_40_out, and_41_out,
       and_42_out, and_43_out, and_44_out, and_45_out, and_46_out, and_47_out, and_48_out, and_49_out,
       and_50_out, and_51_out, and_52_out, and_53_out, and_54_out, and_55_out, and_56_out, and_57_out,
       and_58_out, and_59_out, and_60_out, and_61_out, and_62_out, and_63_out, and_64_out, and_65_out,
       and_66_out, and_67_out, and_68_out, and_69_out, and_70_out, and_71_out, and_72_out, and_73_out,
       and_74_out, and_75_out, and_76_out, and_77_out, and_78_out, and_79_out, and_80_out, and_81_out,
       and_82_out, and_83_out, and_84_out, and_85_out, and_86_out, and_87_out, and_88_out, and_89_out,
       and_90_out, and_91_out, and_92_out, and_93_out, and_94_out, and_95_out, and_96_out, and_97_out,
       and_98_out, and_99_out, and_100_out, and_101_out, and_102_out, and_103_out, and_104_out, and_105_out,
       and_106_out, and_107_out, and_108_out, and_109_out, and_110_out, and_111_out, and_112_out, not_1_out,
       not_2_out, not_3_out, not_4_out, not_5_out, not_6_out, not_7_out, not_8_out, not_9_out, not_10_out,
       not_11_out, not_12_out, not_13_out, not_14_out, not_15_out, not_16_out, not_17_out, not_18_out,
       not_19_out, not_20_out, not_21_out, not_22_out, not_23_out, not_24_out, not_25_out, not_26_out,
       not_27_out, not_28_out, not_29_out, not_30_out, not_31_out, not_32_out, not_33_out, not_34_out,
       not_35_out, not_36_out, not_37_out, not_38_out, not_39_out, not_40_out, not_41_out, not_42_out,
       not_43_out, not_44_out, not_45_out, not_46_out, not_47_out, not_48_out, not_49_out, not_50_out,
       not_51_out, not_52_out, not_53_out, not_54_out, not_55_out, not_56_out, not_57_out, not_58_out,
       not_59_out, not_60_out, not_61_out, not_62_out, not_63_out, not_64_out, not_65_out, not_66_out,
       not_67_out, not_68_out, not_69_out, not_70_out, not_71_out, not_72_out, not_73_out, not_74_out,
       not_75_out, not_76_out, not_77_out, not_78_out, not_79_out, not_80_out, not_81_out, not_82_out,
       or_1_out, or_3_out, or_4_out, or_5_out, or_6_out, or_7_out, or_8_out, or_9_out, or_10_out, or_11_out,
       or_12_out, or_13_out, or_14_out, or_15_out, or_16_out, or_17_out, or_18_out, or_19_out, or_20_out,
       or_21_out;

  not not_1 (not_1_out, in_1[3]);
  not not_2 (not_2_out, in_1[2]);
  not not_3 (not_3_out, in_2[1]);
  not not_4 (not_4_out, in_1[3]);
  not not_5 (not_5_out, in_1[2]);
  not not_6 (not_6_out, in_1[2]);
  not not_7 (not_7_out, in_1[0]);
  not not_8 (not_8_out, in_2[1]);
  not not_9 (not_9_out, in_1[2]);
  not not_10 (not_10_out, in_1[0]);
  not not_11 (not_11_out, in_1[3]);
  not not_12 (not_12_out, in_1[2]);
  not not_13 (not_13_out, in_1[3]);
  not not_14 (not_14_out, in_1[2]);
  not not_15 (not_15_out, in_1[3]);
  not not_16 (not_16_out, in_1[2]);
  not not_17 (not_17_out, in_1[3]);
  not not_18 (not_18_out, in_1[3]);
  not not_19 (not_19_out, in_1[3]);
  not not_20 (not_20_out, in_1[3]);
  not not_21 (not_21_out, in_1[3]);
  not not_22 (not_22_out, in_1[2]);
  not not_23 (not_23_out, in_1[2]);
  not not_24 (not_24_out, in_1[1]);
  not not_25 (not_25_out, in_1[3]);
  not not_26 (not_26_out, in_1[2]);
  not not_27 (not_27_out, in_1[3]);
  not not_28 (not_28_out, in_1[0]);
  not not_29 (not_29_out, in_2[1]);
  and and_1 (and_1_out, not_1_out, not_2_out);
  and and_2 (and_2_out, in_1[0], not_3_out);
  and and_3 (and_3_out, not_4_out, not_5_out);
  and and_4 (and_4_out, in_1[0], in_2[1]);
  not not_30 (not_30_out, in_2[0]);
  and and_5 (and_5_out, in_1[3], not_6_out);
  not not_31 (not_31_out, in_1[1]);
  and and_6 (and_6_out, not_7_out, not_8_out);
  and and_7 (and_7_out, in_1[3], not_9_out);
  not not_32 (not_32_out, in_1[1]);
  and and_8 (and_8_out, not_10_out, in_2[1]);
  not not_33 (not_33_out, in_2[0]);
  not not_34 (not_34_out, in_1[3]);
  not not_35 (not_35_out, in_1[2]);
  not not_36 (not_36_out, in_1[0]);
  and and_9 (and_9_out, not_11_out, not_12_out);
  not not_37 (not_37_out, in_1[1]);
  not not_38 (not_38_out, in_1[0]);
  not not_39 (not_39_out, in_1[3]);
  not not_40 (not_40_out, in_1[2]);
  not not_41 (not_41_out, in_1[3]);
  not not_42 (not_42_out, in_1[2]);
  not not_43 (not_43_out, in_1[3]);
  not not_44 (not_44_out, in_1[3]);
  not not_45 (not_45_out, in_1[3]);
  not not_46 (not_46_out, in_1[2]);
  not not_47 (not_47_out, in_1[0]);
  not not_48 (not_48_out, in_2[1]);
  and and_10 (and_10_out, not_13_out, not_14_out);
  not not_49 (not_49_out, in_1[1]);
  not not_50 (not_50_out, in_2[1]);
  and and_11 (and_11_out, not_15_out, not_16_out);
  not not_51 (not_51_out, in_1[1]);
  and and_12 (and_12_out, not_17_out, in_1[1]);
  not not_52 (not_52_out, in_1[0]);
  not not_53 (not_53_out, in_2[1]);
  not not_54 (not_54_out, in_2[0]);
  and and_13 (and_13_out, not_18_out, in_1[1]);
  not not_55 (not_55_out, in_1[0]);
  and and_14 (and_14_out, not_19_out, in_1[2]);
  not not_56 (not_56_out, in_1[0]);
  not not_57 (not_57_out, in_2[1]);
  and and_15 (and_15_out, not_20_out, in_1[2]);
  not not_58 (not_58_out, in_2[1]);
  not not_59 (not_59_out, in_2[0]);
  not not_60 (not_60_out, in_1[3]);
  not not_61 (not_61_out, in_1[3]);
  not not_62 (not_62_out, in_1[2]);
  not not_63 (not_63_out, in_1[0]);
  not not_64 (not_64_out, in_2[0]);
  and and_16 (and_16_out, not_21_out, not_22_out);
  not not_65 (not_65_out, in_1[1]);
  not not_66 (not_66_out, in_2[1]);
  and and_17 (and_17_out, not_23_out, not_24_out);
  not not_67 (not_67_out, in_1[0]);
  and and_18 (and_18_out, not_25_out, not_26_out);
  not not_68 (not_68_out, in_1[3]);
  not not_69 (not_69_out, in_1[1]);
  not not_70 (not_70_out, in_1[3]);
  not not_71 (not_71_out, in_2[0]);
  not not_72 (not_72_out, in_1[3]);
  and and_19 (and_19_out, not_27_out, in_1[2]);
  and and_20 (and_20_out, not_28_out, not_29_out);
  and and_21 (and_21_out, and_1_out, in_1[1]);
  and and_22 (and_22_out, and_2_out, in_2[0]);
  and and_23 (and_23_out, and_3_out, in_1[1]);
  and and_24 (and_24_out, and_4_out, not_30_out);
  and and_25 (and_25_out, and_5_out, not_31_out);
  and and_26 (and_26_out, and_6_out, in_2[0]);
  and and_27 (and_27_out, and_7_out, not_32_out);
  and and_28 (and_28_out, and_8_out, not_33_out);
  and and_29 (and_29_out, not_34_out, not_35_out);
  and and_30 (and_30_out, not_36_out, in_2[0]);
  and and_31 (and_31_out, and_9_out, not_37_out);
  and and_32 (and_32_out, not_38_out, in_2[1]);
  and and_33 (and_33_out, not_39_out, not_40_out);
  not not_73 (not_73_out, in_1[1]);
  and and_34 (and_34_out, not_41_out, not_42_out);
  not not_74 (not_74_out, in_2[1]);
  not not_75 (not_75_out, in_2[0]);
  and and_35 (and_35_out, not_43_out, in_1[1]);
  not not_76 (not_76_out, in_1[0]);
  and and_36 (and_36_out, not_44_out, in_1[1]);
  not not_77 (not_77_out, in_2[1]);
  not not_78 (not_78_out, in_2[0]);
  not not_79 (not_79_out, in_1[3]);
  and and_37 (and_37_out, not_45_out, in_1[2]);
  not not_80 (not_80_out, in_1[1]);
  and and_38 (and_38_out, in_1[3], not_46_out);
  not not_81 (not_81_out, in_1[1]);
  and and_39 (and_39_out, not_47_out, not_48_out);
  not not_82 (not_82_out, in_2[0]);
  and and_40 (and_40_out, and_10_out, not_49_out);
  and and_41 (and_41_out, in_1[0], not_50_out);
  and and_42 (and_42_out, and_11_out, not_51_out);
  and and_43 (and_43_out, in_1[0], in_2[0]);
  and and_44 (and_44_out, and_12_out, not_52_out);
  and and_45 (and_45_out, not_53_out, not_54_out);
  and and_46 (and_46_out, and_13_out, not_55_out);
  and and_47 (and_47_out, in_2[1], in_2[0]);
  and and_48 (and_48_out, and_14_out, in_1[1]);
  and and_49 (and_49_out, not_56_out, not_57_out);
  and and_50 (and_50_out, and_15_out, in_1[1]);
  and and_51 (and_51_out, not_58_out, not_59_out);
  and and_52 (and_52_out, not_60_out, in_1[2]);
  and and_53 (and_53_out, not_61_out, not_62_out);
  and and_54 (and_54_out, not_63_out, not_64_out);
  and and_55 (and_55_out, and_16_out, not_65_out);
  and and_56 (and_56_out, not_66_out, in_2[0]);
  and and_57 (and_57_out, and_17_out, not_67_out);
  and and_58 (and_58_out, in_2[1], in_2[0]);
  and and_59 (and_59_out, and_18_out, in_1[1]);
  and and_60 (and_60_out, in_2[1], in_2[0]);
  and and_61 (and_61_out, not_68_out, in_1[2]);
  and and_62 (and_62_out, not_69_out, in_1[0]);
  and and_63 (and_63_out, not_70_out, in_1[2]);
  and and_64 (and_64_out, in_1[0], not_71_out);
  and and_65 (and_65_out, not_72_out, in_1[2]);
  and and_66 (and_66_out, in_1[0], in_2[1]);
  and and_67 (and_67_out, and_19_out, in_1[1]);
  and and_68 (and_68_out, and_20_out, in_2[0]);
  and and_69 (and_69_out, and_21_out, and_22_out);
  and and_70 (and_70_out, and_23_out, and_24_out);
  and and_71 (and_71_out, and_25_out, and_26_out);
  and and_72 (and_72_out, and_27_out, and_28_out);
  and and_73 (and_73_out, and_29_out, and_30_out);
  and and_74 (and_74_out, and_31_out, and_32_out);
  and and_75 (and_75_out, and_33_out, not_73_out);
  and and_76 (and_76_out, in_2[1], in_2[0]);
  and and_77 (and_77_out, and_34_out, in_1[1]);
  and and_78 (and_78_out, not_74_out, not_75_out);
  and and_79 (and_79_out, and_35_out, not_76_out);
  and and_80 (and_80_out, in_2[1], in_2[0]);
  and and_81 (and_81_out, and_36_out, in_1[0]);
  and and_82 (and_82_out, not_77_out, not_78_out);
  and and_83 (and_83_out, not_79_out, in_1[2]);
  and and_84 (and_84_out, in_1[0], in_2[0]);
  and and_85 (and_85_out, and_37_out, not_80_out);
  and and_86 (and_86_out, in_1[0], in_2[1]);
  and and_87 (and_87_out, and_38_out, not_81_out);
  and and_88 (and_88_out, and_39_out, not_82_out);
  and and_89 (and_89_out, and_40_out, and_41_out);
  and and_90 (and_90_out, and_42_out, and_43_out);
  and and_91 (and_91_out, and_44_out, and_45_out);
  and and_92 (and_92_out, and_46_out, and_47_out);
  and and_93 (and_93_out, and_48_out, and_49_out);
  and and_94 (and_94_out, and_50_out, and_51_out);
  and and_95 (and_95_out, and_52_out, in_1[1]);
  and and_96 (and_96_out, in_2[1], in_2[0]);
  and and_97 (and_97_out, and_53_out, and_54_out);
  and and_98 (and_98_out, and_55_out, and_56_out);
  and and_99 (and_99_out, and_57_out, and_58_out);
  and and_100 (and_100_out, and_59_out, and_60_out);
  and and_101 (and_101_out, and_61_out, and_62_out);
  and and_102 (and_102_out, and_63_out, and_64_out);
  and and_103 (and_103_out, and_65_out, and_66_out);
  and and_104 (and_104_out, and_67_out, and_68_out);
  or or_1 (or_1_out, and_69_out, and_70_out);
  or or_2 (out_3[3], or_1_out, or_3_out);
  or or_3 (or_3_out, and_71_out, and_72_out);
  or or_4 (or_4_out, and_73_out, and_74_out);
  or or_5 (or_5_out, or_4_out, and_105_out);
  and and_105 (and_105_out, and_75_out, and_76_out);
  and and_106 (and_106_out, and_77_out, and_78_out);
  or or_6 (or_6_out, and_106_out, and_107_out);
  and and_107 (and_107_out, and_79_out, and_80_out);
  and and_108 (and_108_out, and_81_out, and_82_out);
  or or_7 (or_7_out, and_108_out, and_109_out);
  and and_109 (and_109_out, and_83_out, and_84_out);
  and and_110 (and_110_out, and_85_out, and_86_out);
  or or_8 (or_8_out, and_110_out, and_111_out);
  and and_111 (and_111_out, and_87_out, and_88_out);
  or or_9 (or_9_out, and_89_out, and_90_out);
  or or_10 (or_10_out, or_9_out, or_11_out);
  or or_11 (or_11_out, and_91_out, and_92_out);
  or or_12 (or_12_out, and_93_out, and_94_out);
  or or_13 (or_13_out, or_12_out, and_112_out);
  and and_112 (and_112_out, and_95_out, and_96_out);
  or or_14 (or_14_out, and_97_out, and_98_out);
  or or_15 (or_15_out, or_14_out, or_16_out);
  or or_16 (or_16_out, and_99_out, and_100_out);
  or or_17 (or_17_out, and_101_out, and_102_out);
  or or_18 (or_18_out, or_17_out, or_19_out);
  or or_19 (or_19_out, and_103_out, and_104_out);
  or or_20 (or_20_out, or_5_out, or_6_out);
  or or_21 (or_21_out, or_7_out, or_8_out);
  or or_22 (out_3[1], or_10_out, or_13_out);
  or or_23 (out_3[0], or_15_out, or_18_out);
  or or_24 (out_3[2], or_20_out, or_21_out);

  // Other names for the same wires on the sheet: I0 = in_1[0]; I1 = in_1[1]; I2 = in_1[2]; I3 = in_1[3]; D0 = in_2[0];
  //   D1 = in_2[1]; O0 = out_3[0]; O1 = out_3[1]; O2 = out_3[2]; O3 = out_3[3]
endmodule
