// Logisim project ftoi.circ as structural Verilog: 1 circuit, main circuit ftoi
module ftoi (
  input  [15:0] in_1,
  output [31:0] out_2
);

  wire comparator_1_eq, comparator_2_eq, comparator_5_lt, comparator_6_eq, comparator_6_gt, comparator_6_lt,
       multiplexer_1_out, not_1_out, not_2_out, type0, type1, type2;
  wire [4:0] distance, subtractor_1_out, subtractor_2_out;
  wire [31:0] adder_1_out, bit_extender_1_out, bit_extender_2_out, bit_extender_3_out, bit_extender_4_out,
       \input , multiplexer_2_out, multiplexer_3_out, multiplexer_4_out, multiplexer_5_out,
       multiplexer_7_out, multiplier_1_out, \output , shifter_1_out, shifter_2_out, shifter_3_out,
       subtractor_4_out;

  // Probe on out_2
  Comparator #(.width(5), .mode("unsigned")) comparator_1 (
    .a(in_1[14:10]), .b({5{1'b0}}), .eq(comparator_1_eq));  // open: gt, lt
  not not_1 (not_1_out, comparator_1_eq);
  not not_2 (not_2_out, comparator_2_eq);
  Comparator #(.width(5), .mode("unsigned")) comparator_2 (
    .a(in_1[14:10]), .b({5{1'b1}}), .eq(comparator_2_eq));  // open: gt, lt
  Comparator #(.width(5), .mode("unsigned")) comparator_3 (.a(in_1[14:10]), .b({5{1'b0}}), .eq(type1));  // open: gt, lt
  Comparator #(.width(5), .mode("unsigned")) comparator_4 (.a(in_1[14:10]), .b({5{1'b1}}), .eq(type2));  // open: gt, lt
  and and_1 (type0, not_1_out, not_2_out);
  Multiplexer multiplexer_1 (.in0(1'b0), .in1(1'b1), .out(multiplexer_1_out), .sel(type0));  // open: en
  assign bit_extender_1_out = {{31{1'b0}}, multiplexer_1_out};  // Bit_Extender bit_extender_1
  assign bit_extender_2_out = {{31{multiplexer_1_out}}, multiplexer_1_out};  // Bit_Extender bit_extender_2
  assign bit_extender_3_out = {{22{1'b0}}, in_1[9:0]};  // Bit_Extender bit_extender_3
  Subtractor #(.width(5)) subtractor_1 (.a(distance), .b(5'b01010), .out(subtractor_1_out));  // open: bin, bout
  assign bit_extender_4_out = {{22{1'b0}}, in_1[9:0]};  // Bit_Extender bit_extender_4
  Subtractor #(.width(5)) subtractor_2 (.a(5'b01010), .b(distance), .out(subtractor_2_out));  // open: bin, bout
  Multiplexer #(.width(32)) multiplexer_2 (
    .in0(bit_extender_1_out), .in1(bit_extender_2_out), .out(multiplexer_2_out), .sel(in_1[15]));  // open: en
  Shifter #(.width(32)) shifter_1 (.in(32'h1), .\dist (distance), .out(shifter_1_out));
  Shifter #(.width(32)) shifter_2 (.in(bit_extender_3_out), .\dist (subtractor_1_out), .out(shifter_2_out));
  Shifter #(.width(32), .shift("lr")) shifter_3 (
    .in(bit_extender_4_out), .\dist (subtractor_2_out), .out(shifter_3_out));
  Multiplexer #(.width(32)) multiplexer_3 (
    .in0(multiplexer_2_out), .in1({32{1'b0}}), .out(multiplexer_3_out), .sel(type2));  // open: en
  // Probe on distance
  Subtractor #(.width(5)) subtractor_3 (.a(in_1[14:10]), .b(5'b01111), .out(distance));  // open: bin, bout
  Multiplier #(.width(32)) multiplier_1 (.a(\input ), .b(shifter_1_out), .out(multiplier_1_out));  // open: cin, cout
  Comparator #(.width(5), .mode("unsigned")) comparator_5 (
    .a(distance), .b(5'b01010), .lt(comparator_5_lt));  // open: gt, eq
  Comparator #(.width(5)) comparator_6 (
    .a(distance), .b({5{1'b0}}), .gt(comparator_6_gt), .eq(comparator_6_eq), .lt(comparator_6_lt));
  Multiplexer #(.width(32)) multiplexer_4 (
    .in0(shifter_2_out), .in1(shifter_3_out), .out(multiplexer_4_out), .sel(comparator_5_lt));  // open: en
  Multiplexer #(.width(32)) multiplexer_5 (
    .in0(multiplexer_3_out), .in1({32{1'b0}}), .out(multiplexer_5_out), .sel(comparator_6_lt));  // open: en
  Adder #(.width(32)) adder_1 (.a(multiplier_1_out), .b(multiplexer_4_out), .out(adder_1_out));  // open: cin, cout
  Subtractor #(.width(32)) subtractor_4 (
    .a(multiplier_1_out), .b(multiplexer_4_out), .out(subtractor_4_out));  // open: bin, bout
  Multiplexer #(.width(32)) multiplexer_6 (
    .in0(multiplexer_5_out), .in1(multiplexer_7_out), .out(\input ), .sel(comparator_6_eq));  // open: en
  Multiplexer #(.width(32)) multiplexer_7 (
    .in0(32'h1), .in1({32{1'b1}}), .out(multiplexer_7_out), .sel(in_1[15]));  // open: en
  Multiplexer #(.width(32)) multiplexer_8 (
    .in0(adder_1_out), .in1(subtractor_4_out), .out(\output ), .sel(in_1[15]));  // open: en
  Multiplexer #(.width(32)) multiplexer_9 (
    .in0(\input ), .in1(\output ), .out(out_2), .sel(comparator_6_gt));  // open: en

  // Other names for the same wires on the sheet: float[15:0] = in_1; M[9:0] = in_1[9:0]; E[4:0] = in_1[14:10];
  //   S = in_1[15]; int[31:0] = out_2

  // Notes on the sheet:
  //   type为0代表正常，1代表不正常，2代表输出0
endmodule
