// Logisim project 实现GRF.circ as structural Verilog: 1 circuit, main circuit grf
module grf (
  input  clk,
  input  reset,
  input  WE,
  input  [4:0] A1,
  input  [4:0] A2,
  input  [4:0] A3,
  input  [31:0] WD,
  output [31:0] RD1,
  output [31:0] RD2
);

  wire En_0, En_1, En_2, En_3, En_4, En_5, En_6, En_7, En_8, En_9, En_10, En_11, En_12, En_13, En_14, En_15,
       En_16, En_17, En_18, En_19, En_20, En_21, En_22, En_23, En_24, En_25, En_26, En_27, En_28, En_29,
       En_30, En_31;
  wire [31:0] Reg_0, Reg_1, Reg_2, Reg_3, Reg_4, Reg_5, Reg_6, Reg_7, Reg_8, Reg_9, Reg_10, Reg_11, Reg_12,
       Reg_13, Reg_14, Reg_15, Reg_16, Reg_17, Reg_18, Reg_19, Reg_20, Reg_21, Reg_22, Reg_23, Reg_24,
       Reg_25, Reg_26, Reg_27, Reg_28, Reg_29, Reg_30, Reg_31;

  Register #(.width(32)) register_1 (.D({32{1'b0}}), .en(En_0), .Q(Reg_0), .clk(clk), .clr(reset));
  Register #(.width(32)) register_2 (.D(WD), .en(En_8), .Q(Reg_8), .clk(clk), .clr(reset));
  Register #(.width(32)) register_3 (.D(WD), .en(En_16), .Q(Reg_16), .clk(clk), .clr(reset));
  Register #(.width(32)) register_4 (.D(WD), .en(En_24), .Q(Reg_24), .clk(clk), .clr(reset));
  Register #(.width(32)) register_5 (.D(WD), .en(En_1), .Q(Reg_1), .clk(clk), .clr(reset));
  Register #(.width(32)) register_6 (.D(WD), .en(En_9), .Q(Reg_9), .clk(clk), .clr(reset));
  Register #(.width(32)) register_7 (.D(WD), .en(En_17), .Q(Reg_17), .clk(clk), .clr(reset));
  Register #(.width(32)) register_8 (.D(WD), .en(En_25), .Q(Reg_25), .clk(clk), .clr(reset));
  Register #(.width(32)) register_9 (.D(WD), .en(En_2), .Q(Reg_2), .clk(clk), .clr(reset));
  Register #(.width(32)) register_10 (.D(WD), .en(En_10), .Q(Reg_10), .clk(clk), .clr(reset));
  Register #(.width(32)) register_11 (.D(WD), .en(En_18), .Q(Reg_18), .clk(clk), .clr(reset));
  Register #(.width(32)) register_12 (.D(WD), .en(En_26), .Q(Reg_26), .clk(clk), .clr(reset));
  Multiplexer #(.select(5), .width(32)) multiplexer_1 (
    .in0(Reg_0), .in1(Reg_1), .in2(Reg_2), .in3(Reg_3), .in4(Reg_4), .in5(Reg_5), .in6(Reg_6), .in7(Reg_7),
    .in8(Reg_8), .in9(Reg_9), .in10(Reg_10), .in11(Reg_11), .in12(Reg_12), .in13(Reg_13), .in14(Reg_14),
    .in15(Reg_15), .in16(Reg_16), .in17(Reg_17), .in18(Reg_18), .in19(Reg_19), .in20(Reg_20), .in21(Reg_21),
    .in22(Reg_22), .in23(Reg_23), .in24(Reg_24), .in25(Reg_25), .in26(Reg_26), .in27(Reg_27), .in28(Reg_28),
    .in29(Reg_29), .in30(Reg_30), .in31(Reg_31), .out(RD1), .sel(A1));  // open: en
  Register #(.width(32)) register_13 (.D(WD), .en(En_3), .Q(Reg_3), .clk(clk), .clr(reset));
  Register #(.width(32)) register_14 (.D(WD), .en(En_11), .Q(Reg_11), .clk(clk), .clr(reset));
  Register #(.width(32)) register_15 (.D(WD), .en(En_19), .Q(Reg_19), .clk(clk), .clr(reset));
  Register #(.width(32)) register_16 (.D(WD), .en(En_27), .Q(Reg_27), .clk(clk), .clr(reset));
  Multiplexer #(.select(5), .width(32)) multiplexer_2 (
    .in0(Reg_0), .in1(Reg_1), .in2(Reg_2), .in3(Reg_3), .in4(Reg_4), .in5(Reg_5), .in6(Reg_6), .in7(Reg_7),
    .in8(Reg_8), .in9(Reg_9), .in10(Reg_10), .in11(Reg_11), .in12(Reg_12), .in13(Reg_13), .in14(Reg_14),
    .in15(Reg_15), .in16(Reg_16), .in17(Reg_17), .in18(Reg_18), .in19(Reg_19), .in20(Reg_20), .in21(Reg_21),
    .in22(Reg_22), .in23(Reg_23), .in24(Reg_24), .in25(Reg_25), .in26(Reg_26), .in27(Reg_27), .in28(Reg_28),
    .in29(Reg_29), .in30(Reg_30), .in31(Reg_31), .out(RD2), .sel(A2));  // open: en
  Register #(.width(32)) register_17 (.D(WD), .en(En_4), .Q(Reg_4), .clk(clk), .clr(reset));
  Register #(.width(32)) register_18 (.D(WD), .en(En_12), .Q(Reg_12), .clk(clk), .clr(reset));
  Register #(.width(32)) register_19 (.D(WD), .en(En_20), .Q(Reg_20), .clk(clk), .clr(reset));
  Register #(.width(32)) register_20 (.D(WD), .en(En_28), .Q(Reg_28), .clk(clk), .clr(reset));
  Demultiplexer #(.select(5)) demultiplexer_1 (
    .out0(En_0), .out1(En_1), .out2(En_2), .out3(En_3), .out4(En_4), .out5(En_5), .out6(En_6), .out7(En_7),
    .out8(En_8), .out9(En_9), .out10(En_10), .out11(En_11), .out12(En_12), .out13(En_13), .out14(En_14),
    .out15(En_15), .out16(En_16), .out17(En_17), .out18(En_18), .out19(En_19), .out20(En_20), .out21(En_21),
    .out22(En_22), .out23(En_23), .out24(En_24), .out25(En_25), .out26(En_26), .out27(En_27), .out28(En_28),
    .out29(En_29), .out30(En_30), .out31(En_31), .in(WE), .sel(A3));  // open: en
  Register #(.width(32)) register_21 (.D(WD), .en(En_5), .Q(Reg_5), .clk(clk), .clr(reset));
  Register #(.width(32)) register_22 (.D(WD), .en(En_13), .Q(Reg_13), .clk(clk), .clr(reset));
  Register #(.width(32)) register_23 (.D(WD), .en(En_21), .Q(Reg_21), .clk(clk), .clr(reset));
  Register #(.width(32)) register_24 (.D(WD), .en(En_29), .Q(Reg_29), .clk(clk), .clr(reset));
  Register #(.width(32)) register_25 (.D(WD), .en(En_6), .Q(Reg_6), .clk(clk), .clr(reset));
  Register #(.width(32)) register_26 (.D(WD), .en(En_14), .Q(Reg_14), .clk(clk), .clr(reset));
  Register #(.width(32)) register_27 (.D(WD), .en(En_22), .Q(Reg_22), .clk(clk), .clr(reset));
  Register #(.width(32)) register_28 (.D(WD), .en(En_30), .Q(Reg_30), .clk(clk), .clr(reset));
  Register #(.width(32)) register_29 (.D(WD), .en(En_7), .Q(Reg_7), .clk(clk), .clr(reset));
  Register #(.width(32)) register_30 (.D(WD), .en(En_15), .Q(Reg_15), .clk(clk), .clr(reset));
  Register #(.width(32)) register_31 (.D(WD), .en(En_23), .Q(Reg_23), .clk(clk), .clr(reset));
  Register #(.width(32)) register_32 (.D(WD), .en(En_31), .Q(Reg_31), .clk(clk), .clr(reset));
endmodule
