// Logisim project main - v0.0.circ as structural Verilog: 8 circuits, main circuit main
module main (
  input  in_1
);

  wire AluSrc, beq, clk, eq, RegDst, SignExt, WeDm, WeGrf;
  wire [1:0] WhichtoReg;
  wire [2:0] AluOp;
  wire [4:0] MemAddr, multiplexer_1_out, rd, rs, rt, shamt;
  wire [5:0] func, op;
  wire [15:0] imm16;
  wire [25:0] addr;
  wire [31:0] GrfRead1, GrfRead2, imm32, instr, MemRead, multiplexer_2_out, multiplexer_3_out, Res;

  Clock clock_1 (.out(clk));
  // Probe on instr
  Multiplexer #(.width(5)) multiplexer_1 (.in0(rd), .in1(rt), .out(multiplexer_1_out), .sel(RegDst));  // open: en
  Multiplexer #(.select(2), .width(32)) multiplexer_2 (
    .in0({Res[31:7], MemAddr, Res[1:0]}), .in1(MemRead), .in2({imm16, {16{1'b0}}}), .out(multiplexer_2_out),
    .sel(WhichtoReg));  // open: in3, en
  Splitter splitter_1 (
    .in_1(instr), .out_2(op), .out_3(rs), .out_4(rt), .out_5(rd), .out_6(shamt), .out_7(func), .out_8(imm16),
    .out_9(addr));
  IFU ifu_1 (.reset(in_1), .beq(beq), .eq(eq), .imm32(imm32), .out_6(instr), .clk(clk));
  Multiplexer #(.width(32)) multiplexer_3 (
    .in0(GrfRead2), .in1(imm32), .out(multiplexer_3_out), .sel(AluSrc));  // open: en
  GRF grf_1 (
    .clk(clk), .reset(in_1), .WE(WeGrf), .A1(rs), .A2(rt), .A3(multiplexer_1_out), .WD(multiplexer_2_out),
    .RD1(GrfRead1), .RD2(GrfRead2));
  ALU alu_1 (.A(GrfRead1), .B(multiplexer_3_out), .in_3(AluOp), .eq(eq), .res({Res[31:7], MemAddr, Res[1:0]}));
  EXT ext_1 (.imm16(imm16), .sign(SignExt), .imm32(imm32));
  Controller controller_1 (
    .op(op), .func(func), .AluOp(AluOp), .WeGrf(WeGrf), .WeDm(WeDm), .beq(beq), .AluSrc(AluSrc),
    .WhichtoReg(WhichtoReg), .RegDst(RegDst), .SignExt(SignExt));
  DM dm_1 (.clk(clk), .reset(in_1), .WE(WeDm), .A(MemAddr), .WD(GrfRead2), .RD(MemRead));

  // Other names for the same wires on the sheet: Res[6:2] = MemAddr; reset = in_1
endmodule

module GRF (
  input  clk,
  input  reset,
  input  WE,
  input  [4:0] A1,
  input  [4:0] A2,
  input  [4:0] A3,
  input  [31:0] WD,
  output [31:0] RD1,
  output [31:0] RD2
);

  wire En_0, En_1, En_2, En_3, En_4, En_5, En_6, En_7, En_8, En_9, En_10, En_11, En_12, En_13, En_14, En_15,
       En_16, En_17, En_18, En_19, En_20, En_21, En_22, En_23, En_24, En_25, En_26, En_27, En_28, En_29,
       En_30, En_31;
  wire [31:0] Reg_0, Reg_1, Reg_2, Reg_3, Reg_4, Reg_5, Reg_6, Reg_7, Reg_8, Reg_9, Reg_10, Reg_11, Reg_12,
       Reg_13, Reg_14, Reg_15, Reg_16, Reg_17, Reg_18, Reg_19, Reg_20, Reg_21, Reg_22, Reg_23, Reg_24,
       Reg_25, Reg_26, Reg_27, Reg_28, Reg_29, Reg_30, Reg_31;

  Register #(.width(32)) register_1 (.D({32{1'b0}}), .en(En_0), .Q(Reg_0), .clk(clk), .clr(reset));
  Register #(.width(32)) register_2 (.D(WD), .en(En_8), .Q(Reg_8), .clk(clk), .clr(reset));
  Register #(.width(32)) register_3 (.D(WD), .en(En_16), .Q(Reg_16), .clk(clk), .clr(reset));
  Register #(.width(32)) register_4 (.D(WD), .en(En_24), .Q(Reg_24), .clk(clk), .clr(reset));
  Register #(.width(32)) register_5 (.D(WD), .en(En_1), .Q(Reg_1), .clk(clk), .clr(reset));
  Register #(.width(32)) register_6 (.D(WD), .en(En_9), .Q(Reg_9), .clk(clk), .clr(reset));
  Register #(.width(32)) register_7 (.D(WD), .en(En_17), .Q(Reg_17), .clk(clk), .clr(reset));
  Register #(.width(32)) register_8 (.D(WD), .en(En_25), .Q(Reg_25), .clk(clk), .clr(reset));
  Register #(.width(32)) register_9 (.D(WD), .en(En_2), .Q(Reg_2), .clk(clk), .clr(reset));
  Register #(.width(32)) register_10 (.D(WD), .en(En_10), .Q(Reg_10), .clk(clk), .clr(reset));
  Register #(.width(32)) register_11 (.D(WD), .en(En_18), .Q(Reg_18), .clk(clk), .clr(reset));
  Register #(.width(32)) register_12 (.D(WD), .en(En_26), .Q(Reg_26), .clk(clk), .clr(reset));
  Multiplexer #(.select(5), .width(32)) multiplexer_1 (
    .in0(Reg_0), .in1(Reg_1), .in2(Reg_2), .in3(Reg_3), .in4(Reg_4), .in5(Reg_5), .in6(Reg_6), .in7(Reg_7),
    .in8(Reg_8), .in9(Reg_9), .in10(Reg_10), .in11(Reg_11), .in12(Reg_12), .in13(Reg_13), .in14(Reg_14),
    .in15(Reg_15), .in16(Reg_16), .in17(Reg_17), .in18(Reg_18), .in19(Reg_19), .in20(Reg_20), .in21(Reg_21),
    .in22(Reg_22), .in23(Reg_23), .in24(Reg_24), .in25(Reg_25), .in26(Reg_26), .in27(Reg_27), .in28(Reg_28),
    .in29(Reg_29), .in30(Reg_30), .in31(Reg_31), .out(RD1), .sel(A1));  // open: en
  Register #(.width(32)) register_13 (.D(WD), .en(En_3), .Q(Reg_3), .clk(clk), .clr(reset));
  Register #(.width(32)) register_14 (.D(WD), .en(En_11), .Q(Reg_11), .clk(clk), .clr(reset));
  Register #(.width(32)) register_15 (.D(WD), .en(En_19), .Q(Reg_19), .clk(clk), .clr(reset));
  Register #(.width(32)) register_16 (.D(WD), .en(En_27), .Q(Reg_27), .clk(clk), .clr(reset));
  Multiplexer #(.select(5), .width(32)) multiplexer_2 (
    .in0(Reg_0), .in1(Reg_1), .in2(Reg_2), .in3(Reg_3), .in4(Reg_4), .in5(Reg_5), .in6(Reg_6), .in7(Reg_7),
    .in8(Reg_8), .in9(Reg_9), .in10(Reg_10), .in11(Reg_11), .in12(Reg_12), .in13(Reg_13), .in14(Reg_14),
    .in15(Reg_15), .in16(Reg_16), .in17(Reg_17), .in18(Reg_18), .in19(Reg_19), .in20(Reg_20), .in21(Reg_21),
    .in22(Reg_22), .in23(Reg_23), .in24(Reg_24), .in25(Reg_25), .in26(Reg_26), .in27(Reg_27), .in28(Reg_28),
    .in29(Reg_29), .in30(Reg_30), .in31(Reg_31), .out(RD2), .sel(A2));  // open: en
  Register #(.width(32)) register_17 (.D(WD), .en(En_4), .Q(Reg_4), .clk(clk), .clr(reset));
  Register #(.width(32)) register_18 (.D(WD), .en(En_12), .Q(Reg_12), .clk(clk), .clr(reset));
  Register #(.width(32)) register_19 (.D(WD), .en(En_20), .Q(Reg_20), .clk(clk), .clr(reset));
  Register #(.width(32)) register_20 (.D(WD), .en(En_28), .Q(Reg_28), .clk(clk), .clr(reset));
  Demultiplexer #(.select(5)) demultiplexer_1 (
    .out0(En_0), .out1(En_1), .out2(En_2), .out3(En_3), .out4(En_4), .out5(En_5), .out6(En_6), .out7(En_7),
    .out8(En_8), .out9(En_9), .out10(En_10), .out11(En_11), .out12(En_12), .out13(En_13), .out14(En_14),
    .out15(En_15), .out16(En_16), .out17(En_17), .out18(En_18), .out19(En_19), .out20(En_20), .out21(En_21),
    .out22(En_22), .out23(En_23), .out24(En_24), .out25(En_25), .out26(En_26), .out27(En_27), .out28(En_28),
    .out29(En_29), .out30(En_30), .out31(En_31), .in(WE), .sel(A3));  // open: en
  Register #(.width(32)) register_21 (.D(WD), .en(En_5), .Q(Reg_5), .clk(clk), .clr(reset));
  Register #(.width(32)) register_22 (.D(WD), .en(En_13), .Q(Reg_13), .clk(clk), .clr(reset));
  Register #(.width(32)) register_23 (.D(WD), .en(En_21), .Q(Reg_21), .clk(clk), .clr(reset));
  Register #(.width(32)) register_24 (.D(WD), .en(En_29), .Q(Reg_29), .clk(clk), .clr(reset));
  Register #(.width(32)) register_25 (.D(WD), .en(En_6), .Q(Reg_6), .clk(clk), .clr(reset));
  Register #(.width(32)) register_26 (.D(WD), .en(En_14), .Q(Reg_14), .clk(clk), .clr(reset));
  Register #(.width(32)) register_27 (.D(WD), .en(En_22), .Q(Reg_22), .clk(clk), .clr(reset));
  Register #(.width(32)) register_28 (.D(WD), .en(En_30), .Q(Reg_30), .clk(clk), .clr(reset));
  Register #(.width(32)) register_29 (.D(WD), .en(En_7), .Q(Reg_7), .clk(clk), .clr(reset));
  Register #(.width(32)) register_30 (.D(WD), .en(En_15), .Q(Reg_15), .clk(clk), .clr(reset));
  Register #(.width(32)) register_31 (.D(WD), .en(En_23), .Q(Reg_23), .clk(clk), .clr(reset));
  Register #(.width(32)) register_32 (.D(WD), .en(En_31), .Q(Reg_31), .clk(clk), .clr(reset));
endmodule

module Splitter (
  input  [31:0] in_1,
  output [5:0] out_2,
  output [4:0] out_3,
  output [4:0] out_4,
  output [4:0] out_5,
  output [4:0] out_6,
  output [5:0] out_7,
  output [15:0] out_8,
  output [25:0] out_9
);


  assign out_2 = in_1[31:26];
  assign out_3 = in_1[25:21];
  assign out_4 = in_1[20:16];
  assign out_5 = in_1[15:11];
  assign out_6 = in_1[10:6];
  assign out_7 = in_1[5:0];
  assign out_8 = in_1[15:0];
  assign out_9 = in_1[25:0];

  // Other names for the same wires on the sheet: addr[25:0] = in_1[25:0]; func[5:0] = in_1[5:0];
  //   imm16[15:0] = in_1[15:0]; instr[31:0] = in_1; shamt[4:0] = in_1[10:6]; rd[4:0] = in_1[15:11];
  //   rt[4:0] = in_1[20:16]; rs[4:0] = in_1[25:21]; op[5:0] = in_1[31:26]
endmodule

module ALU (
  input  [31:0] A,
  input  [31:0] B,
  input  [2:0] in_3,
  output eq,
  output [31:0] res
);

  wire [31:0] adder_1_out, and_1_out, or_1_out, subtractor_1_out;

  Comparator #(.width(32), .mode("unsigned")) comparator_1 (.a(A), .b(B), .eq(eq));  // open: gt, lt
  Adder #(.width(32)) adder_1 (.a(A), .b(B), .out(adder_1_out));  // open: cin, cout
  Subtractor #(.width(32)) subtractor_1 (.a(A), .b(B), .out(subtractor_1_out));  // open: bin, bout
  assign and_1_out = A & B;  // AND_Gate and_1, 32 bits wide
  assign or_1_out = A | B;  // OR_Gate or_1, 32 bits wide
  Multiplexer #(.select(3), .width(32)) multiplexer_1 (
    .in0(adder_1_out), .in1(subtractor_1_out), .in2(and_1_out), .in3(or_1_out), .out(res), .sel(in_3));  // open: in4, in5, in6, in7, en

  // Other names for the same wires on the sheet: ALUop[2:0] = in_3
endmodule

module EXT (
  input  [15:0] imm16,
  input  sign,
  output [31:0] imm32
);

  wire [31:0] bit_extender_1_out, bit_extender_2_out;

  assign bit_extender_1_out = {{16{1'b0}}, imm16};  // Bit_Extender bit_extender_1
  assign bit_extender_2_out = {{16{imm16[15]}}, imm16};  // Bit_Extender bit_extender_2
  Multiplexer #(.width(32)) multiplexer_1 (
    .in0(bit_extender_1_out), .in1(bit_extender_2_out), .out(imm32), .sel(sign));  // open: en
endmodule

module IFU (
  input  clk,
  input  reset,
  input  beq,
  input  eq,
  input  [31:0] imm32,
  output [31:0] out_6
);

  wire and_1_out;
  wire [31:0] adder_1_out, adder_2_out, NPC, PC, shifter_1_out;

  Register #(.width(32)) register_1 (.D(NPC), .Q(PC), .clk(clk), .clr(reset));  // open: en
  Adder #(.width(32)) adder_1 (.a(PC), .b(32'h4), .out(adder_1_out));  // open: cin, cout
  Shifter #(.width(32)) shifter_1 (.in(imm32), .\dist (5'b00010), .out(shifter_1_out));
  Adder #(.width(32)) adder_2 (.a(adder_1_out), .b(shifter_1_out), .out(adder_2_out));  // open: cin, cout
  ROM #(.addrWidth(5), .dataWidth(32)) rom_1 (.addr(PC[6:2]), .data(out_6));  // open: sel
  Multiplexer #(.width(32)) multiplexer_1 (
    .in0(adder_1_out), .in1(adder_2_out), .out(NPC), .sel(and_1_out));  // open: en
  and and_1 (and_1_out, beq, eq);

  // Other names for the same wires on the sheet: instr[31:0] = out_6

  // Notes on the sheet:
  //   contents of rom_1 (hex, n*v repeats v):
  //   341c0000 341d0000 340080f8 36ee0367 3593769c 34dda539 3465c5dc 34be0ff1 3472af1d 35566602 35fe72a7
  //   3437ff23 37b9649e 3690bf9b 37fe4e0c 3711f49d 3c113bfe 3c057433 3c03c451 3c04c431 3c1c24d9 3c1bf0da
  //   3c0ccc68 3c0a118d 3c1021ea 3c0004d3 3c16115b 3c184f06 3c1215de 1000ffff
endmodule

module Controller (
  input  [5:0] op,
  input  [5:0] func,
  output [1:0] WhichtoReg,
  output [2:0] AluOp,
  output WeGrf,
  output WeDm,
  output beq,
  output AluSrc,
  output RegDst,
  output SignExt
);

  wire addu, beq_t, lui, lw, not_1_out, not_2_out, not_3_out, not_4_out, not_5_out, not_6_out, not_7_out,
       not_8_out, not_9_out, not_10_out, not_11_out, not_12_out, ori, R, subu, sw;

  not not_1 (not_1_out, op[4]);
  not not_2 (not_2_out, op[5]);
  not not_3 (not_3_out, op[2]);
  not not_4 (not_4_out, op[3]);
  not not_5 (not_5_out, op[1]);
  not not_6 (not_6_out, op[0]);
  not not_7 (not_7_out, func[5]);
  not not_8 (not_8_out, func[3]);
  not not_9 (not_9_out, func[4]);
  not not_10 (not_10_out, func[1]);
  not not_11 (not_11_out, func[2]);
  not not_12 (not_12_out, func[0]);
  and u_R (R, not_2_out, not_1_out, not_4_out, not_3_out, not_5_out, not_6_out);
  and and_1 (addu, R, func[5], not_9_out, not_8_out, not_11_out, not_10_out, func[0]);
  and and_2 (subu, R, func[5], not_9_out, not_8_out, not_11_out, func[1], func[0]);
  and and_3 (ori, not_2_out, not_1_out, op[3], op[2], not_5_out, op[0]);
  and and_4 (lw, op[5], not_1_out, not_4_out, not_3_out, op[1], op[0]);
  and and_5 (sw, op[5], not_1_out, op[3], not_3_out, op[1], op[0]);
  and and_6 (lui, not_2_out, not_1_out, op[3], op[2], op[1], op[0]);
  and and_7 (beq_t, not_2_out, not_1_out, not_4_out, op[2], not_5_out, not_6_out);
  buf or_1 (AluOp[2], 1'b0);  // OR_Gate
  buf or_2 (AluOp[1], ori);  // OR_Gate
  or or_3 (AluOp[0], subu, ori);
  or or_4 (WeGrf, addu, subu, ori, lw, lui);
  buf or_5 (WeDm, sw);  // OR_Gate
  buf or_6 (beq, beq_t);  // OR_Gate
  or or_7 (AluSrc, ori, lw, lui, sw);
  buf or_8 (WhichtoReg[1], lui);  // OR_Gate
  buf or_9 (WhichtoReg[0], lw);  // OR_Gate
  or or_10 (RegDst, ori, lw, sw, lui, beq_t);
  or or_11 (SignExt, lw, sw, beq_t);
endmodule

module DM (
  input  clk,
  input  reset,
  input  WE,
  input  [4:0] A,
  input  [31:0] WD,
  output [31:0] RD
);

  RAM #(.addrWidth(5), .dataWidth(32), .bus("separate")) ram_1 (
    .addr(A), .din(WD), .data(RD), .str(WE), .clk(clk), .clr(reset));  // open: sel, ld
endmodule
