// Logisim project main - v1.1.circ as structural Verilog: 8 circuits, main circuit main
module main (
  input  in_1,
  output [31:0] instr,
  output RegWrite,
  output [4:0] RegAddr,
  output [31:0] RegData,
  output MemWrite,
  output [4:0] MemAddr,
  output [31:0] MemData
);

  wire ALUSrc, clk, IsBeq, IsEq, IsSignExt, RegDst;
  wire [1:0] WhichToReg;
  wire [2:0] ALUOp;
  wire [4:0] rd, rs, rt, shamt;
  wire [5:0] func, op;
  wire [15:0] imm16;
  wire [25:0] addr;
  wire [31:0] DmRead, GrfRead1, imm32, multiplexer_3_out, Res;

  Clock clock_1 (.out(clk));
  Multiplexer #(.width(5)) multiplexer_1 (.in0(rd), .in1(rt), .out(RegAddr), .sel(RegDst));  // open: en
  // Probe on instr
  Multiplexer #(.select(2), .width(32)) multiplexer_2 (
    .in0({Res[31:7], MemAddr, Res[1:0]}), .in1(DmRead), .in2({imm16, {16{1'b0}}}), .out(RegData),
    .sel(WhichToReg));  // open: in3, en
  Splitter splitter_1 (
    .in_1(instr), .out_2(op), .out_3(rs), .out_4(rt), .out_5(rd), .out_6(shamt), .out_7(func), .out_8(imm16),
    .out_9(addr));
  IFU ifu_1 (.reset(in_1), .IsBeq(IsBeq), .IsEq(IsEq), .imm32(imm32), .out_6(instr), .clk(clk));
  Multiplexer #(.width(32)) multiplexer_3 (
    .in0(MemData), .in1(imm32), .out(multiplexer_3_out), .sel(ALUSrc));  // open: en
  GRF grf_1 (
    .clk(clk), .reset(in_1), .WeGrf(RegWrite), .rs(rs), .rt(rt), .rd(RegAddr), .GrfWrite(RegData),
    .GrfRead1(GrfRead1), .GrfRead2(MemData));
  ALU alu_1 (.A(GrfRead1), .B(multiplexer_3_out), .in_3(ALUOp), .IsEq(IsEq), .res({Res[31:7], MemAddr, Res[1:0]}));
  EXT ext_1 (.imm16(imm16), .IsSignExt(IsSignExt), .imm32(imm32));
  Controller controller_1 (
    .op(op), .func(func), .ALUOp(ALUOp), .WeGrf(RegWrite), .WeDm(MemWrite), .IsBeq(IsBeq), .ALUSrc(ALUSrc),
    .WhichToReg(WhichToReg), .RegDst(RegDst), .IsSignExt(IsSignExt));
  DM dm_1 (.clk(clk), .reset(in_1), .WeDm(MemWrite), .DmWriteAddr(MemAddr), .DmWrite(MemData), .RD(DmRead));

  // Other names for the same wires on the sheet: GrfRead2[31:0] = MemData; RegWriteAddr[4:0] = RegAddr;
  //   DmWriteAddr[4:0] = MemAddr; Res[6:2] = MemAddr; reset = in_1; WeDm = MemWrite; WeGrf = RegWrite
endmodule

module GRF (
  input  clk,
  input  reset,
  input  WeGrf,
  input  [4:0] rs,
  input  [4:0] rt,
  input  [4:0] rd,
  input  [31:0] GrfWrite,
  output [31:0] GrfRead1,
  output [31:0] GrfRead2
);

  wire En_0, En_1, En_2, En_3, En_4, En_5, En_6, En_7, En_8, En_9, En_10, En_11, En_12, En_13, En_14, En_15,
       En_16, En_17, En_18, En_19, En_20, En_21, En_22, En_23, En_24, En_25, En_26, En_27, En_28, En_29,
       En_30, En_31;
  wire [31:0] Reg_0, Reg_1, Reg_2, Reg_3, Reg_4, Reg_5, Reg_6, Reg_7, Reg_8, Reg_9, Reg_10, Reg_11, Reg_12,
       Reg_13, Reg_14, Reg_15, Reg_16, Reg_17, Reg_18, Reg_19, Reg_20, Reg_21, Reg_22, Reg_23, Reg_24,
       Reg_25, Reg_26, Reg_27, Reg_28, Reg_29, Reg_30, Reg_31;

  Register #(.width(32)) register_1 (.D({32{1'b0}}), .en(En_0), .Q(Reg_0), .clk(clk), .clr(reset));
  Register #(.width(32)) register_2 (.D(GrfWrite), .en(En_8), .Q(Reg_8), .clk(clk), .clr(reset));
  Register #(.width(32)) register_3 (.D(GrfWrite), .en(En_16), .Q(Reg_16), .clk(clk), .clr(reset));
  Register #(.width(32)) register_4 (.D(GrfWrite), .en(En_24), .Q(Reg_24), .clk(clk), .clr(reset));
  Register #(.width(32)) register_5 (.D(GrfWrite), .en(En_1), .Q(Reg_1), .clk(clk), .clr(reset));
  Register #(.width(32)) register_6 (.D(GrfWrite), .en(En_9), .Q(Reg_9), .clk(clk), .clr(reset));
  Register #(.width(32)) register_7 (.D(GrfWrite), .en(En_17), .Q(Reg_17), .clk(clk), .clr(reset));
  Register #(.width(32)) register_8 (.D(GrfWrite), .en(En_25), .Q(Reg_25), .clk(clk), .clr(reset));
  Register #(.width(32)) register_9 (.D(GrfWrite), .en(En_2), .Q(Reg_2), .clk(clk), .clr(reset));
  Register #(.width(32)) register_10 (.D(GrfWrite), .en(En_10), .Q(Reg_10), .clk(clk), .clr(reset));
  Register #(.width(32)) register_11 (.D(GrfWrite), .en(En_18), .Q(Reg_18), .clk(clk), .clr(reset));
  Register #(.width(32)) register_12 (.D(GrfWrite), .en(En_26), .Q(Reg_26), .clk(clk), .clr(reset));
  Multiplexer #(.select(5), .width(32)) multiplexer_1 (
    .in0(Reg_0), .in1(Reg_1), .in2(Reg_2), .in3(Reg_3), .in4(Reg_4), .in5(Reg_5), .in6(Reg_6), .in7(Reg_7),
    .in8(Reg_8), .in9(Reg_9), .in10(Reg_10), .in11(Reg_11), .in12(Reg_12), .in13(Reg_13), .in14(Reg_14),
    .in15(Reg_15), .in16(Reg_16), .in17(Reg_17), .in18(Reg_18), .in19(Reg_19), .in20(Reg_20), .in21(Reg_21),
    .in22(Reg_22), .in23(Reg_23), .in24(Reg_24), .in25(Reg_25), .in26(Reg_26), .in27(Reg_27), .in28(Reg_28),
    .in29(Reg_29), .in30(Reg_30), .in31(Reg_31), .out(GrfRead1), .sel(rs));  // open: en
  Register #(.width(32)) register_13 (.D(GrfWrite), .en(En_3), .Q(Reg_3), .clk(clk), .clr(reset));
  Register #(.width(32)) register_14 (.D(GrfWrite), .en(En_11), .Q(Reg_11), .clk(clk), .clr(reset));
  Register #(.width(32)) register_15 (.D(GrfWrite), .en(En_19), .Q(Reg_19), .clk(clk), .clr(reset));
  Register #(.width(32)) register_16 (.D(GrfWrite), .en(En_27), .Q(Reg_27), .clk(clk), .clr(reset));
  Register #(.width(32)) register_17 (.D(GrfWrite), .en(En_4), .Q(Reg_4), .clk(clk), .clr(reset));
  Register #(.width(32)) register_18 (.D(GrfWrite), .en(En_12), .Q(Reg_12), .clk(clk), .clr(reset));
  Register #(.width(32)) register_19 (.D(GrfWrite), .en(En_20), .Q(Reg_20), .clk(clk), .clr(reset));
  Register #(.width(32)) register_20 (.D(GrfWrite), .en(En_28), .Q(Reg_28), .clk(clk), .clr(reset));
  Multiplexer #(.select(5), .width(32)) multiplexer_2 (
    .in0(Reg_0), .in1(Reg_1), .in2(Reg_2), .in3(Reg_3), .in4(Reg_4), .in5(Reg_5), .in6(Reg_6), .in7(Reg_7),
    .in8(Reg_8), .in9(Reg_9), .in10(Reg_10), .in11(Reg_11), .in12(Reg_12), .in13(Reg_13), .in14(Reg_14),
    .in15(Reg_15), .in16(Reg_16), .in17(Reg_17), .in18(Reg_18), .in19(Reg_19), .in20(Reg_20), .in21(Reg_21),
    .in22(Reg_22), .in23(Reg_23), .in24(Reg_24), .in25(Reg_25), .in26(Reg_26), .in27(Reg_27), .in28(Reg_28),
    .in29(Reg_29), .in30(Reg_30), .in31(Reg_31), .out(GrfRead2), .sel(rt));  // open: en
  Register #(.width(32)) register_21 (.D(GrfWrite), .en(En_5), .Q(Reg_5), .clk(clk), .clr(reset));
  Register #(.width(32)) register_22 (.D(GrfWrite), .en(En_13), .Q(Reg_13), .clk(clk), .clr(reset));
  Register #(.width(32)) register_23 (.D(GrfWrite), .en(En_21), .Q(Reg_21), .clk(clk), .clr(reset));
  Register #(.width(32)) register_24 (.D(GrfWrite), .en(En_29), .Q(Reg_29), .clk(clk), .clr(reset));
  Demultiplexer #(.select(5)) demultiplexer_1 (
    .out0(En_0), .out1(En_1), .out2(En_2), .out3(En_3), .out4(En_4), .out5(En_5), .out6(En_6), .out7(En_7),
    .out8(En_8), .out9(En_9), .out10(En_10), .out11(En_11), .out12(En_12), .out13(En_13), .out14(En_14),
    .out15(En_15), .out16(En_16), .out17(En_17), .out18(En_18), .out19(En_19), .out20(En_20), .out21(En_21),
    .out22(En_22), .out23(En_23), .out24(En_24), .out25(En_25), .out26(En_26), .out27(En_27), .out28(En_28),
    .out29(En_29), .out30(En_30), .out31(En_31), .in(WeGrf), .sel(rd));  // open: en
  Register #(.width(32)) register_25 (.D(GrfWrite), .en(En_6), .Q(Reg_6), .clk(clk), .clr(reset));
  Register #(.width(32)) register_26 (.D(GrfWrite), .en(En_14), .Q(Reg_14), .clk(clk), .clr(reset));
  Register #(.width(32)) register_27 (.D(GrfWrite), .en(En_22), .Q(Reg_22), .clk(clk), .clr(reset));
  Register #(.width(32)) register_28 (.D(GrfWrite), .en(En_30), .Q(Reg_30), .clk(clk), .clr(reset));
  Register #(.width(32)) register_29 (.D(GrfWrite), .en(En_7), .Q(Reg_7), .clk(clk), .clr(reset));
  Register #(.width(32)) register_30 (.D(GrfWrite), .en(En_15), .Q(Reg_15), .clk(clk), .clr(reset));
  Register #(.width(32)) register_31 (.D(GrfWrite), .en(En_23), .Q(Reg_23), .clk(clk), .clr(reset));
  Register #(.width(32)) register_32 (.D(GrfWrite), .en(En_31), .Q(Reg_31), .clk(clk), .clr(reset));
endmodule

module Splitter (
  input  [31:0] in_1,
  output [5:0] out_2,
  output [4:0] out_3,
  output [4:0] out_4,
  output [4:0] out_5,
  output [4:0] out_6,
  output [5:0] out_7,
  output [15:0] out_8,
  output [25:0] out_9
);


  assign out_2 = in_1[31:26];
  assign out_3 = in_1[25:21];
  assign out_4 = in_1[20:16];
  assign out_5 = in_1[15:11];
  assign out_6 = in_1[10:6];
  assign out_7 = in_1[5:0];
  assign out_8 = in_1[15:0];
  assign out_9 = in_1[25:0];

  // Other names for the same wires on the sheet: addr[25:0] = in_1[25:0]; func[5:0] = in_1[5:0];
  //   imm16[15:0] = in_1[15:0]; instr[31:0] = in_1; shamt[4:0] = in_1[10:6]; rd[4:0] = in_1[15:11];
  //   rt[4:0] = in_1[20:16]; rs[4:0] = in_1[25:21]; op[5:0] = in_1[31:26]
endmodule

module ALU (
  input  [31:0] A,
  input  [31:0] B,
  input  [2:0] in_3,
  output IsEq,
  output [31:0] res
);

  wire [31:0] adder_1_out, and_1_out, or_1_out, subtractor_1_out;

  Adder #(.width(32)) adder_1 (.a(A), .b(B), .out(adder_1_out));  // open: cin, cout
  Subtractor #(.width(32)) subtractor_1 (.a(A), .b(B), .out(subtractor_1_out));  // open: bin, bout
  assign and_1_out = A & B;  // AND_Gate and_1, 32 bits wide
  assign or_1_out = A | B;  // OR_Gate or_1, 32 bits wide
  Comparator #(.width(32), .mode("unsigned")) comparator_1 (.a(A), .b(B), .eq(IsEq));  // open: gt, lt
  Multiplexer #(.select(3), .width(32)) multiplexer_1 (
    .in0(adder_1_out), .in1(subtractor_1_out), .in2(and_1_out), .in3(or_1_out), .out(res), .sel(in_3));  // open: in4, in5, in6, in7, en

  // Other names for the same wires on the sheet: ALUop[2:0] = in_3; ALURead1[31:0] = A; ALURead2[31:0] = B
endmodule

module EXT (
  input  [15:0] imm16,
  input  IsSignExt,
  output [31:0] imm32
);

  wire [31:0] bit_extender_1_out, bit_extender_2_out;

  assign bit_extender_1_out = {{16{1'b0}}, imm16};  // Bit_Extender bit_extender_1
  assign bit_extender_2_out = {{16{imm16[15]}}, imm16};  // Bit_Extender bit_extender_2
  Multiplexer #(.width(32)) multiplexer_1 (
    .in0(bit_extender_1_out), .in1(bit_extender_2_out), .out(imm32), .sel(IsSignExt));  // open: en
endmodule

module IFU (
  input  clk,
  input  reset,
  input  IsBeq,
  input  IsEq,
  input  [31:0] imm32,
  output [31:0] out_6
);

  wire and_1_out;
  wire [31:0] adder_1_out, adder_2_out, NPC, PC, shifter_1_out;

  Register #(.width(32)) register_1 (.D(NPC), .Q(PC), .clk(clk), .clr(reset));  // open: en
  Adder #(.width(32)) adder_1 (.a(PC), .b(32'h4), .out(adder_1_out));  // open: cin, cout
  Shifter #(.width(32)) shifter_1 (.in(imm32), .\dist (5'b00010), .out(shifter_1_out));
  Adder #(.width(32)) adder_2 (.a(adder_1_out), .b(shifter_1_out), .out(adder_2_out));  // open: cin, cout
  ROM #(.addrWidth(5), .dataWidth(32)) rom_1 (.addr(PC[6:2]), .data(out_6));  // open: sel
  Multiplexer #(.width(32)) multiplexer_1 (
    .in0(adder_1_out), .in1(adder_2_out), .out(NPC), .sel(and_1_out));  // open: en
  and and_1 (and_1_out, IsBeq, IsEq);

  // Other names for the same wires on the sheet: instr[31:0] = out_6
endmodule

module Controller (
  input  [5:0] op,
  input  [5:0] func,
  output [1:0] WhichToReg,
  output [2:0] ALUOp,
  output WeGrf,
  output WeDm,
  output IsBeq,
  output ALUSrc,
  output RegDst,
  output IsSignExt
);

  wire addu, beq, lui, lw, not_1_out, not_2_out, not_3_out, not_4_out, not_5_out, not_6_out, not_7_out,
       not_8_out, not_9_out, not_10_out, not_11_out, not_12_out, ori, R, subu, sw;

  not not_1 (not_1_out, op[5]);
  not not_2 (not_2_out, op[4]);
  not not_3 (not_3_out, op[3]);
  not not_4 (not_4_out, op[2]);
  not not_5 (not_5_out, op[0]);
  not not_6 (not_6_out, op[1]);
  not not_7 (not_7_out, func[5]);
  not not_8 (not_8_out, func[4]);
  not not_9 (not_9_out, func[3]);
  not not_10 (not_10_out, func[1]);
  not not_11 (not_11_out, func[2]);
  not not_12 (not_12_out, func[0]);
  and u_R (R, not_1_out, not_2_out, not_3_out, not_4_out, not_6_out, not_5_out);
  and and_1 (addu, R, func[5], not_8_out, not_9_out, not_11_out, not_10_out, func[0]);
  and and_2 (subu, R, func[5], not_8_out, not_9_out, not_11_out, func[1], func[0]);
  and and_3 (ori, not_1_out, not_2_out, op[3], op[2], not_6_out, op[0]);
  and and_4 (lw, op[5], not_2_out, not_3_out, not_4_out, op[1], op[0]);
  and and_5 (sw, op[5], not_2_out, op[3], not_4_out, op[1], op[0]);
  and and_6 (lui, not_1_out, not_2_out, op[3], op[2], op[1], op[0]);
  and and_7 (beq, not_1_out, not_2_out, not_3_out, op[2], not_6_out, not_5_out);
  buf or_1 (ALUOp[2], 1'b0);  // OR_Gate
  buf or_2 (ALUOp[1], ori);  // OR_Gate
  or or_3 (ALUOp[0], subu, ori);
  or or_4 (WeGrf, addu, subu, ori, lw, lui);
  buf or_5 (WeDm, sw);  // OR_Gate
  buf or_6 (IsBeq, beq);  // OR_Gate
  or or_7 (ALUSrc, ori, lw, lui, sw);
  buf or_8 (WhichToReg[1], lui);  // OR_Gate
  buf or_9 (WhichToReg[0], lw);  // OR_Gate
  or or_10 (RegDst, ori, lw, sw, lui, beq);
  or or_11 (IsSignExt, lw, sw, beq);
endmodule

module DM (
  input  clk,
  input  reset,
  input  WeDm,
  input  [4:0] DmWriteAddr,
  input  [31:0] DmWrite,
  output [31:0] RD
);

  RAM #(.addrWidth(5), .dataWidth(32), .bus("separate")) ram_1 (
    .addr(DmWriteAddr), .din(DmWrite), .data(RD), .str(WeDm), .clk(clk), .clr(reset));  // open: sel, ld

  // Other names for the same wires on the sheet: DmRead[31:0] = RD
endmodule
